# Fritzing sketch wiring (saved by Fritzing 0.9.3b)
perfboards: 1

parts:
  U1 = NodeMCU V3.0
  SD_card_module1 = SD Card Module
  Bauteil1 = Adafruit MAX98357A I2S 3W Class D Amplifier [part_number="Adafruit #3006"]
  SP1 = SPEAKER [package=pcb_mount_speaker]
  R1 = Resistor [tolerance=±5% resistance=20k package=THT]
  R3 = Resistor [tolerance=±5% resistance=2.2k package=THT]
  R4 = Resistor [tolerance=±5% resistance=3.3k package=THT]
  R5 = Resistor [tolerance=±5% resistance=4.7k package=THT]
  R6 = Resistor [tolerance=±5% resistance=5.11k package=THT]
  R7 = Resistor [tolerance=±5% resistance=6.8k package=THT]
  R8 = Resistor [tolerance=±5% resistance=10.13k package=THT]
  R2 = Resistor [tolerance=±5% resistance=2k package=THT]
  J1 = female pin header, 9 pins [form="♀ (female)"]
  J2 = female pin header, 9 pins [form="♀ (female)"]
  R9 = Resistor [tolerance=±5% resistance=10k package=THT]
  R10 = Resistor [tolerance=±5% resistance=10k package=THT]

nets:
  N1: U1.D0, SD_card_module1.CS
  N2: U1.D4, Bauteil1.LRCLK
  N3: U1.3V3, SD_card_module1.+3.3
  GND: U1.GND#6, U1.GND#13, U1.GND#16, U1.GND#33, SD_card_module1.GND, Bauteil1.GND
  N4: U1.D5, SD_card_module1.SCK
  N5: U1.D6, SD_card_module1.MISO
  N6: U1.D7, SD_card_module1.MOSI
  N7: U1.D8, Bauteil1.BCLK
  N8: U1.RX, Bauteil1.DIN
  VIN: U1.Vin, Bauteil1.VIN, R1.Pin_1
  N9: U1.GND#41, U1.A0, R1.Pin_0, R2.Pin_1, J1.pin9, J2.pin9
  N10: Bauteil1.VO-, SP1.+
  N11: Bauteil1.VO+, SP1.-
  N12: R3.Pin_0, R4.Pin_1, J1.pin7, J2.pin7
  N13: R3.Pin_1, R2.Pin_0, J1.pin8
  N14: R4.Pin_0, R5.Pin_1, J1.pin6, J2.pin6
  N15: R5.Pin_0, R6.Pin_1, J1.pin5
  N16: R6.Pin_0, R7.Pin_1, J1.pin4
  N17: R7.Pin_0, R8.Pin_1, J1.pin3, J2.pin3
  N18: R8.Pin_0, J1.pin2, R9.Pin_1
  N19: J1.pin1, R9.Pin_0, R10.Pin_1

custom parts:
  NodeMCU V3.0: ESP8266 based NodeMCU
  SD Card Module: SD Card Module Slot Socket Reader For Arduino ARM MCU
  Adafruit MAX98357A I2S 3W Class D Amplifier: Listen to this good news - we now have an all in one digital audio amp breakout board that works incredibly well with the Raspberry Pi! If you're looking for an easy and low cost way to get you digital sound files bumpin' then the MAX08357 I2S Amp Breakout is for you. It takes standard I2S digital audio input and, not only decodes it into analog, but also amplifies it directly into a speaker.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
